# Fritzing sketch dew_point_fan (saved by Fritzing 0.9.6b)
breadboards: 1

parts:
  Raspberry_Pi2 = Raspberry Pi B rev2
  LCD2004-I2C2 = LCD2004-I2C
  Bauteil1 = Solid State High Level Relay Module [package=relay]
  R1 = Resistor [tolerance=±5% resistance=1k package="0402 [SMD]"]
  R2 = Resistor [tolerance=±5% resistance=10k package="0402 [SMD]"]
  R3 = Resistor [tolerance=±5% resistance=100 package="0402 [SMD]"]
  Ein_-_Auto_-_Aus = Slide_SW_micro_dpdt
  DHT-Innen = DHT22 Humidity and Temperature Sensor
  DHT-Außen = DHT22 Humidity and Temperature Sensor
  R4 = Resistor [tolerance=±5% resistance=100 package="0402 [SMD]"]
  R5 = Resistor [tolerance=±5% resistance=10k package="0402 [SMD]"]
  C3 = Capacitor Polarized [package=cpol-radial-1000uf-25v]
  C4 = Ceramic Capacitor [capacitance=100nF voltage=35V package="200 mil [THT, multilayer]"]

nets:
  VDD: Raspberry_Pi2.3V3, Raspberry_Pi2.5V, LCD2004-I2C2.VCC, Bauteil1.DC+, R2.Pin_1, R3.Pin_1, DHT-Innen.VDD, DHT-Außen.VDD, R5.Pin_1, C3.+, C4.1
  N1: Raspberry_Pi2.GPIO_2, LCD2004-I2C2.SDA
  N2: Raspberry_Pi2.GPIO_3, LCD2004-I2C2.SCL
  GND: Raspberry_Pi2.GND, LCD2004-I2C2.GND, Bauteil1.DC-, DHT-Innen.GND, DHT-Außen.GND, R4.Pin_1, C3.-, C4.0
  N3: Raspberry_Pi2.GPIO_23, DHT-Außen.DATA, R5.Pin_0
  N4: Raspberry_Pi2.GPIO_22, Bauteil1.CH1, R1.Pin_1, Ein_-_Auto_-_Aus.pin_1
  N5: Raspberry_Pi2.GPIO_24, R2.Pin_0, DHT-Innen.DATA
  N6: Raspberry_Pi2.GPIO_25, R1.Pin_0
  N7: R3.Pin_0, Ein_-_Auto_-_Aus.pin_2
  N8: Ein_-_Auto_-_Aus.pin_3, R4.Pin_0

custom parts:
  LCD2004-I2C: A standard character display with 4x20 characters. Comes in many colors with LCM2004 IIC attached.
  Solid State High Level Relay Module: 5V Omron solid state relay 240V 2A output with resistance fuse.
  Slide_SW_micro_dpdt: silver mico switch
